// Logisim project cpu.circ as structural Verilog: 6 circuits, main circuit main
module main (
  input  [31:0] INSTRUCTION,
  input  CLOCK,
  output [31:0] FETCH_ADDRESS,
  output [31:0] ra,
  output [31:0] sp,
  output [31:0] t0,
  output [31:0] t1,
  output [31:0] t2,
  output [31:0] s0,
  output [31:0] s1,
  output [31:0] a0
);

  wire ASel, brEQ, brLT, brUN, BSel, jump, lwc_en, memWE, PCsel, regWE;
  wire [1:0] WBSel;
  wire [3:0] ALUSel;
  wire [4:0] rd, rs1, rs2;
  wire [31:0] alu_result, DMEM_p5, immGen, multiplexer_1_out, multiplexer_2_out, multiplexer_3_out,
       multiplexer_4_out, multiplexer_5_out, pc, pc2, pc2add4, pcadd4, R1, R2, register_1_q,
       stack_instruction_1_instruction_trans;

  Adder #(.width(32)) adder_1 (.a(pc), .b(32'h4), .out(pcadd4));  // open: cin, cout
  Multiplexer #(.width(32), .enable("false")) multiplexer_1 (
    .in0(pcadd4), .in1(alu_result), .out(multiplexer_1_out), .sel(PCsel));
  // Probe on pcadd4
  // Probe on multiplexer_1_out
  Register #(.width(32)) register_1 (.D(multiplexer_2_out), .clk(CLOCK), .Q(register_1_q));  // open: en, clr
  Multiplexer #(.width(32), .enable("false")) multiplexer_2 (
    .in0(INSTRUCTION), .in1({32{1'b0}}), .out(multiplexer_2_out), .sel(jump));
  Shifter #(.width(32), .shift("lr")) shifter_1 (.in(pc), .\dist (5'b00010), .out(FETCH_ADDRESS));
  Register #(.width(32)) u_PC (.D(multiplexer_1_out), .clk(CLOCK), .Q(pc));  // open: en, clr
  // Probe on pc
  // Probe on alu_result
  Adder #(.width(32)) adder_2 (.a(pc2), .b(32'h4), .out(pc2add4));  // open: cin, cout
  stack_instruction stack_instruction_1 (
    .instruction(register_1_q), .instruction_trans(stack_instruction_1_instruction_trans));
  // Probe on regWE
  // Probe on multiplexer_5_out
  control_unit control_unit_1 (
    .INSTRUCTION(stack_instruction_1_instruction_trans), .brEQ(brEQ), .brLT(brLT), .lwc_en(lwc_en),
    .rs1(rs1), .rs2(rs2), .rd(rd), .brUN(brUN), .Asel(ASel), .PCsel(PCsel), .Bsel(BSel), .jump(jump),
    .ALUSel(ALUSel), .MEM_WE(memWE), .regWE(regWE), .WBsel(WBSel), .immediate(immGen));  // open: loadbyte, loadhalf, out_20
  // regfile_main RegFile: pin names not known; wires that end beside it: t0, t1, t2, s0, s1, a0, R1, R2
  Register #(.width(32)) register_2 (.D(pc), .clk(CLOCK), .Q(pc2));  // open: en, clr
  // Probe on pc2
  Multiplexer #(.width(32), .enable("false")) multiplexer_3 (
    .in0(R2), .in1(immGen), .out(multiplexer_3_out), .sel(BSel));
  // Probe on immGen
  // Probe on multiplexer_4_out
  Multiplexer #(.width(32), .enable("false")) multiplexer_4 (.in0(R1), .in1(pc2), .out(multiplexer_4_out), .sel(ASel));
  // Probe on t1
  // alu Arithmetic_Logic_Unit: pin names not known; wires that end beside it: multiplexer_4_out, multiplexer_3_out, ALUSel, alu_result
  // Probe on alu_result
  // Probe on alu_result
  branchcom branchcom_1 (.R1(R1), .R2(R2), .brUN(brUN), .brEQ(brEQ), .brLT(brLT));
  // Probe on immGen
  lwc_com lwc_com_1 (.R2(R2), .lwc_en(lwc_en));
  // Probe on pc2add4
  // mem_main DMEM: pin names not known; wires that end beside it: alu_result, R2, memWE, CLOCK, DMEM_p5
  // Probe on DMEM_p5
  Multiplexer #(.select(2), .width(32), .enable("false")) multiplexer_5 (
    .in0(pc2add4), .in1(alu_result), .in2(DMEM_p5), .out(multiplexer_5_out), .sel(WBSel));  // open: in3

  // Other names for the same wires on the sheet: clk = CLOCK; PROGRAM_COUNTER[31:0] = pc

  // Notes on the sheet:
  //   Output
  //   Inputs/Outputs from run.circ. DO NOT MOVE THESE.
  //   Inputs
  //   It is OK to move the PC, RegFile, ALU, and MEM to wherever is most convenient for you when constructing your CPU, and to delete this text
  //   Inputs/Outputs from run.circ. DO NOT MOVE THESE.
endmodule

module immGen1 (
  input  [24:0] Limm,
  input  [24:0] Simm,
  input  [24:0] SBimm,
  input  [24:0] Uimm,
  input  [2:0] ImmSel,
  input  [24:0] UJimm,
  output [31:0] ImmGen
);

  wire [31:0] bit_extender_1_out, bit_extender_2_out, bit_extender_3_out, bit_extender_4_out;

  assign bit_extender_1_out = {{20{Limm[24]}}, Limm[24:13]};  // Bit_Extender bit_extender_1
  assign bit_extender_2_out = {{20{Simm[24]}}, {Simm[24:18], Simm[4:0]}};  // Bit_Extender bit_extender_2
  assign bit_extender_3_out = {{19{SBimm[24]}}, {SBimm[24], SBimm[0], SBimm[23:18], SBimm[4:1], 1'b0}};  // Bit_Extender bit_extender_3
  assign bit_extender_4_out = {{11{UJimm[24]}}, {UJimm[24], UJimm[12:5], UJimm[13], UJimm[23:14], 1'b0}};  // Bit_Extender bit_extender_4
  Multiplexer #(.select(3), .width(32)) multiplexer_1 (
    .in0(bit_extender_1_out), .in1(bit_extender_2_out), .in2(bit_extender_3_out),
    .in3({Uimm[24:5], {12{1'b0}}}), .in4(bit_extender_4_out), .out(ImmGen), .sel(ImmSel));  // open: in5, in6, in7, en
endmodule

module branchcom (
  input  [31:0] R1,
  input  [31:0] R2,
  input  brUN,
  output brEQ,
  output brLT
);

  wire comparator_1_lt, comparator_2_lt;

  Comparator #(.width(32)) comparator_1 (.a(R1), .b(R2), .eq(brEQ), .lt(comparator_1_lt));  // open: gt
  Comparator #(.width(32), .mode("unsigned")) comparator_2 (.a(R1), .b(R2), .lt(comparator_2_lt));  // open: gt, eq
  Multiplexer #(.enable("false")) multiplexer_1 (.in0(comparator_1_lt), .in1(comparator_2_lt), .out(brLT), .sel(brUN));

  // Other names for the same wires on the sheet: A[31:0] = R1; B[31:0] = R2
endmodule

module control_unit (
  input  [31:0] INSTRUCTION,
  input  brEQ,
  input  brLT,
  input  lwc_en,
  output [4:0] rs1,
  output loadbyte,
  output [4:0] rs2,
  output loadhalf,
  output [4:0] rd,
  output brUN,
  output Asel,
  output PCsel,
  output Bsel,
  output jump,
  output [3:0] ALUSel,
  output MEM_WE,
  output regWE,
  output [1:0] WBsel,
  output [31:0] immediate,
  output out_20
);

  wire ADD_0, AND_1, and_1_out, and_2_out, and_3_out, and_4_out, and_5_out, and_46_out, and_47_out,
       and_48_out, and_49_out, BSEL_13, comparator_9_eq, comparator_10_eq, comparator_11_eq,
       comparator_12_eq, DIVU_8, f7_00, f7_01, f7_20, fun3_0, fun3_1, fun3_2, fun3_3, fun3_4, fun3_5, fun3_6,
       fun3_7, I03, I13, I67, i_addi, i_andi, i_jalr, i_lw, i_lwc, i_ori, i_slli, i_slti, i_srai, i_srli,
       i_xori, MULH_14, MULHU_11, MULT_10, normal_I03, or_1_out, OR_2, or_7_out, or_8_out, or_15_out,
       or_17_out, R, r_add, r_and, r_or, r_remu, r_sll, r_slt, r_srl, r_sub, r_xor, S, SB, sb_beq, sb_blt,
       sb_bne, SLL_6, SLT_7, SRL_4, UJ, XOR_3;
  wire [1:0] and_43_out, and_44_out, and_45_out, bit_extender_13_out, bit_extender_14_out,
       bit_extender_15_out;
  wire [3:0] and_50_out, and_51_out, and_52_out, and_53_out, and_54_out, and_55_out, and_56_out, and_57_out,
       and_58_out, and_59_out, and_60_out, and_61_out, and_62_out, and_63_out, and_64_out,
       bit_extender_16_out, bit_extender_17_out, bit_extender_18_out, bit_extender_19_out,
       bit_extender_20_out, bit_extender_21_out, bit_extender_22_out, bit_extender_23_out,
       bit_extender_24_out, bit_extender_25_out, bit_extender_26_out, bit_extender_27_out,
       bit_extender_28_out, bit_extender_29_out, bit_extender_30_out;
  wire [11:0] bit_extender_4_out, bit_extender_5_out;
  wire [19:0] bit_extender_3_out;
  wire [20:0] bit_extender_1_out, bit_extender_2_out;
  wire [31:0] and_20_out, and_21_out, and_22_out, and_23_out, and_24_out, and_25_out, bit_extender_6_out,
       bit_extender_7_out, bit_extender_8_out, bit_extender_9_out, bit_extender_10_out, bit_extender_11_out,
       bit_extender_12_out;

  assign bit_extender_1_out = {{20{INSTRUCTION[31]}}, INSTRUCTION[31]};  // Bit_Extender bit_extender_1
  assign bit_extender_2_out = {{20{INSTRUCTION[31]}}, INSTRUCTION[31]};  // Bit_Extender bit_extender_2
  assign bit_extender_3_out = {{19{INSTRUCTION[31]}}, INSTRUCTION[31]};  // Bit_Extender bit_extender_3
  assign bit_extender_4_out = {{11{INSTRUCTION[31]}}, INSTRUCTION[31]};  // Bit_Extender bit_extender_4
  and u_and_1 (and_1_out, i_lwc, lwc_en);
  assign bit_extender_5_out = {{11{1'b0}}, 1'b0};  // Bit_Extender bit_extender_5
  or or_1 (or_1_out, normal_I03, I13, I67);
  assign bit_extender_6_out = {{25{INSTRUCTION[31]}}, INSTRUCTION[31:25]};  // Bit_Extender bit_extender_6
  assign bit_extender_7_out = {{31{i_lwc}}, i_lwc};  // Bit_Extender bit_extender_7
  and and_2 (and_2_out, sb_beq, brEQ);
  and and_3 (and_3_out, sb_blt, brLT);
  and and_4 (and_4_out, brUN, brLT);
  and and_5 (and_5_out, sb_bne, ~brEQ);  // AND_Gate
  or u_or_2 (regWE, I13, R, normal_I03, and_1_out, I67, BSEL_13, UJ);
  and and_6 (r_add, R, fun3_0, f7_00);
  and and_7 (MULT_10, R, fun3_0, f7_01);
  and and_8 (r_sub, R, fun3_0, f7_20);
  and and_9 (r_sll, R, fun3_1, f7_00);
  and and_10 (MULH_14, R, fun3_1, f7_01);
  and and_11 (MULHU_11, R, fun3_3, f7_01);
  and and_12 (r_slt, R, fun3_2, f7_00);
  and and_13 (r_xor, R, fun3_4, f7_00);
  and and_14 (DIVU_8, R, fun3_5, f7_01);
  and and_15 (r_srl, R, fun3_5, f7_00);
  and and_16 (r_or, R, fun3_6, f7_00);
  and and_17 (r_remu, R, fun3_7, f7_01);
  and and_18 (r_and, R, fun3_7, f7_00);
  and and_19 (MEM_WE, S, fun3_2);
  assign bit_extender_8_out = {{31{or_1_out}}, or_1_out};  // Bit_Extender bit_extender_8
  assign bit_extender_9_out = {{31{S}}, S};  // Bit_Extender bit_extender_9
  assign bit_extender_10_out = {{31{SB}}, SB};  // Bit_Extender bit_extender_10
  assign bit_extender_11_out = {{31{BSEL_13}}, BSEL_13};  // Bit_Extender bit_extender_11
  assign bit_extender_12_out = {{31{UJ}}, UJ};  // Bit_Extender bit_extender_12
  // Probe on regWE
  assign and_20_out = {bit_extender_1_out, INSTRUCTION[30:20]} & bit_extender_8_out;  // AND_Gate and_20, 32 bits wide
  assign and_21_out = {bit_extender_2_out, INSTRUCTION[30:25], INSTRUCTION[11:7]} & bit_extender_9_out;  // AND_Gate and_21, 32 bits wide
  assign and_22_out = {bit_extender_3_out, INSTRUCTION[7], INSTRUCTION[30:25], INSTRUCTION[11:8], 1'b0} & bit_extender_10_out;  // AND_Gate and_22, 32 bits wide
  assign and_23_out = {INSTRUCTION[31:12], bit_extender_5_out} & bit_extender_11_out;  // AND_Gate and_23, 32 bits wide
  assign and_24_out = {bit_extender_4_out, INSTRUCTION[19:12], INSTRUCTION[20], INSTRUCTION[30:21], 1'b0} & bit_extender_12_out;  // AND_Gate and_24, 32 bits wide
  assign and_25_out = bit_extender_6_out & bit_extender_7_out;  // AND_Gate and_25, 32 bits wide
  or or_3 (jump, UJ, i_jalr, and_2_out, and_3_out, and_4_out, and_5_out);
  Comparator #(.width(7)) comparator_1 (.a(INSTRUCTION[6:0]), .b(7'b0110011), .eq(R));  // open: gt, lt
  Comparator #(.width(7)) comparator_2 (.a(INSTRUCTION[6:0]), .b(7'b0000011), .eq(I03));  // open: gt, lt
  Comparator #(.width(7)) comparator_3 (.a(INSTRUCTION[6:0]), .b(7'b0010011), .eq(I13));  // open: gt, lt
  Comparator #(.width(7)) comparator_4 (.a(INSTRUCTION[6:0]), .b(7'b0100011), .eq(S));  // open: gt, lt
  Comparator #(.width(7)) comparator_5 (.a(INSTRUCTION[6:0]), .b(7'b1100011), .eq(SB));  // open: gt, lt
  Comparator #(.width(7)) comparator_6 (.a(INSTRUCTION[6:0]), .b(7'b0110111), .eq(BSEL_13));  // open: gt, lt
  Comparator #(.width(7)) comparator_7 (.a(INSTRUCTION[6:0]), .b(7'b1101111), .eq(UJ));  // open: gt, lt
  Comparator #(.width(7)) comparator_8 (.a(INSTRUCTION[6:0]), .b(7'b1100111), .eq(I67));  // open: gt, lt
  assign immediate = and_20_out | and_21_out | and_22_out | and_23_out | and_24_out | and_25_out;  // OR_Gate or_4, 32 bits wide
  // Probe on immediate
  Comparator #(.width(3), .mode("unsigned")) comparator_9 (
    .a(INSTRUCTION[14:12]), .b(3'b000), .eq(comparator_9_eq));  // open: gt, lt
  Comparator #(.width(3), .mode("unsigned")) comparator_10 (
    .a(INSTRUCTION[14:12]), .b(3'b001), .eq(comparator_10_eq));  // open: gt, lt
  Comparator #(.width(3), .mode("unsigned")) comparator_11 (
    .a(INSTRUCTION[14:12]), .b(3'b010), .eq(comparator_11_eq));  // open: gt, lt
  Comparator #(.width(3), .mode("unsigned")) comparator_12 (
    .a(INSTRUCTION[14:12]), .b(3'b111), .eq(comparator_12_eq));  // open: gt, lt
  or or_5 (normal_I03, loadbyte, loadhalf, i_lw);
  Decoder #(.select(3), .enable("false")) decoder_1 (
    .out0(fun3_0), .out1(fun3_1), .out2(fun3_2), .out3(fun3_3), .out4(fun3_4), .out5(fun3_5), .out6(fun3_6),
    .out7(fun3_7), .sel(INSTRUCTION[14:12]));
  Decoder #(.select(3), .enable("false")) decoder_2 (
    .out0(fun3_0), .out1(fun3_1), .out2(fun3_2), .out3(fun3_3), .out4(fun3_4), .out5(fun3_5), .out6(fun3_6),
    .out7(fun3_7), .sel(INSTRUCTION[14:12]));
  and and_26 (i_addi, I13, fun3_0);
  and and_27 (i_slli, I13, fun3_1, f7_00);
  and and_28 (i_slti, I13, fun3_2);
  and and_29 (i_xori, I13, fun3_4);
  and and_30 (i_srli, I13, fun3_5, f7_00);
  and and_31 (i_srai, I13, fun3_5, f7_20);
  and and_32 (i_ori, I13, fun3_6);
  and and_33 (i_andi, I13, fun3_7);
  and and_34 (i_jalr, I67, fun3_0);
  and and_35 (sb_beq, SB, fun3_0);
  and and_36 (sb_blt, SB, fun3_4);
  and and_37 (brUN, SB, fun3_6);
  and and_38 (sb_bne, SB, fun3_1);
  // Probe on INSTRUCTION[31:25]
  Comparator #(.width(7)) comparator_13 (.a(INSTRUCTION[31:25]), .b({7{1'b0}}), .eq(f7_00));  // open: gt, lt
  Comparator #(.width(7)) comparator_14 (.a(INSTRUCTION[31:25]), .b(7'b0000001), .eq(f7_01));  // open: gt, lt
  Comparator #(.width(7)) comparator_15 (.a(INSTRUCTION[31:25]), .b(7'b0100000), .eq(f7_20));  // open: gt, lt
  and and_39 (loadbyte, I03, comparator_9_eq);
  and and_40 (loadhalf, I03, comparator_10_eq);
  and and_41 (i_lw, I03, comparator_11_eq);
  and and_42 (i_lwc, I03, comparator_12_eq);
  or or_6 (ADD_0, r_add, loadbyte, loadhalf, i_lw, i_addi, MEM_WE, i_lwc, sb_beq, sb_blt, brUN, sb_bne, UJ, i_jalr);
  or or_7 (or_7_out, normal_I03, i_lwc);
  or or_8 (or_8_out, I67, UJ);
  or or_9 (AND_1, r_and, i_andi);
  or or_10 (OR_2, r_or, i_ori);
  or or_11 (XOR_3, r_xor, i_xori);
  or or_12 (SRL_4, r_srl, i_srli);
  or or_13 (SLL_6, r_sll, i_slli);
  or or_14 (SLT_7, i_slti, r_slt);
  assign bit_extender_13_out = {{1{or_15_out}}, or_15_out};  // Bit_Extender bit_extender_13
  or or_15 (or_15_out, I13, R, BSEL_13, out_20);
  assign bit_extender_14_out = {{1{or_7_out}}, or_7_out};  // Bit_Extender bit_extender_14
  assign bit_extender_15_out = {{1{or_8_out}}, or_8_out};  // Bit_Extender bit_extender_15
  Comparator #(.width(32)) comparator_16 (.a(INSTRUCTION), .b({32{1'b0}}), .eq(out_20));  // open: gt, lt
  assign and_43_out = bit_extender_13_out & 2'b01;  // AND_Gate and_43, 2 bits wide
  assign and_44_out = bit_extender_14_out & 2'b10;  // AND_Gate and_44, 2 bits wide
  assign and_45_out = bit_extender_15_out & 2'b00;  // AND_Gate and_45, 2 bits wide
  not not_1 (Bsel, R);
  not not_2 (Bsel, R);
  assign WBsel = and_43_out | and_44_out | and_45_out;  // OR_Gate or_16, 2 bits wide
  // Probe on WBsel
  and and_46 (and_46_out, sb_beq, brEQ);
  and and_47 (and_47_out, sb_blt, brLT);
  and and_48 (and_48_out, brUN, brLT);
  and and_49 (and_49_out, sb_bne, ~brEQ);  // AND_Gate
  assign bit_extender_16_out = {{3{ADD_0}}, ADD_0};  // Bit_Extender bit_extender_16
  assign bit_extender_17_out = {{3{AND_1}}, AND_1};  // Bit_Extender bit_extender_17
  assign bit_extender_18_out = {{3{OR_2}}, OR_2};  // Bit_Extender bit_extender_18
  assign bit_extender_19_out = {{3{XOR_3}}, XOR_3};  // Bit_Extender bit_extender_19
  assign bit_extender_20_out = {{3{SRL_4}}, SRL_4};  // Bit_Extender bit_extender_20
  assign bit_extender_21_out = {{3{i_srai}}, i_srai};  // Bit_Extender bit_extender_21
  assign bit_extender_22_out = {{3{SLL_6}}, SLL_6};  // Bit_Extender bit_extender_22
  assign bit_extender_23_out = {{3{SLT_7}}, SLT_7};  // Bit_Extender bit_extender_23
  assign bit_extender_24_out = {{3{DIVU_8}}, DIVU_8};  // Bit_Extender bit_extender_24
  assign bit_extender_25_out = {{3{r_remu}}, r_remu};  // Bit_Extender bit_extender_25
  assign bit_extender_26_out = {{3{MULT_10}}, MULT_10};  // Bit_Extender bit_extender_26
  assign bit_extender_27_out = {{3{MULHU_11}}, MULHU_11};  // Bit_Extender bit_extender_27
  assign bit_extender_28_out = {{3{r_sub}}, r_sub};  // Bit_Extender bit_extender_28
  assign bit_extender_29_out = {{3{BSEL_13}}, BSEL_13};  // Bit_Extender bit_extender_29
  assign bit_extender_30_out = {{3{MULH_14}}, MULH_14};  // Bit_Extender bit_extender_30
  not not_3 (Asel, or_17_out);
  or or_17 (or_17_out, i_lwc, R, normal_I03, I13, S, I67);
  assign and_50_out = bit_extender_16_out & 4'b0000;  // AND_Gate and_50, 4 bits wide
  assign and_51_out = bit_extender_17_out & 4'b0001;  // AND_Gate and_51, 4 bits wide
  assign and_52_out = bit_extender_18_out & 4'b0010;  // AND_Gate and_52, 4 bits wide
  assign and_53_out = bit_extender_19_out & 4'b0011;  // AND_Gate and_53, 4 bits wide
  assign and_54_out = bit_extender_20_out & 4'b0100;  // AND_Gate and_54, 4 bits wide
  assign and_55_out = bit_extender_21_out & 4'b0101;  // AND_Gate and_55, 4 bits wide
  assign and_56_out = bit_extender_22_out & 4'b0110;  // AND_Gate and_56, 4 bits wide
  assign and_57_out = bit_extender_23_out & 4'b0111;  // AND_Gate and_57, 4 bits wide
  assign and_58_out = bit_extender_24_out & 4'b1000;  // AND_Gate and_58, 4 bits wide
  assign and_59_out = bit_extender_25_out & 4'b1001;  // AND_Gate and_59, 4 bits wide
  assign and_60_out = bit_extender_26_out & 4'b1010;  // AND_Gate and_60, 4 bits wide
  assign and_61_out = bit_extender_27_out & 4'b1011;  // AND_Gate and_61, 4 bits wide
  assign and_62_out = bit_extender_28_out & 4'b1100;  // AND_Gate and_62, 4 bits wide
  assign and_63_out = bit_extender_29_out & 4'b1101;  // AND_Gate and_63, 4 bits wide
  assign and_64_out = bit_extender_30_out & 4'b1110;  // AND_Gate and_64, 4 bits wide
  or or_18 (PCsel, and_46_out, and_47_out, and_48_out, and_49_out, UJ, i_jalr);
  assign ALUSel = and_50_out | and_51_out | and_52_out | and_53_out | and_54_out | and_55_out | and_56_out | and_57_out | and_58_out | and_59_out | and_60_out | and_61_out | and_62_out | and_63_out | and_64_out;  // OR_Gate or_19, 4 bits wide

  assign rd = INSTRUCTION[11:7];
  assign rs1 = INSTRUCTION[19:15];
  assign rs2 = INSTRUCTION[24:20];

  // Other names for the same wires on the sheet: ins_11_7[4:0] = INSTRUCTION[11:7]; ins_11_8[3:0] = INSTRUCTION[11:8];
  //   ins_7 = INSTRUCTION[7]; func7[6:0] = INSTRUCTION[31:25]; ins_31 = INSTRUCTION[31];
  //   ins_31_12[19:0] = INSTRUCTION[31:12]; ins_31_20[11:0] = INSTRUCTION[31:20]; func3[2:0] = INSTRUCTION[14:12];
  //   ins_19_12[7:0] = INSTRUCTION[19:12]; i_lb = loadbyte; i_lh = loadhalf; SRA_5 = i_srai; ins_20 = INSTRUCTION[20];
  //   ins_30_20[10:0] = INSTRUCTION[30:20]; ins_30_21[9:0] = INSTRUCTION[30:21]; ins_30_25[5:0] = INSTRUCTION[30:25];
  //   intype[6:0] = INSTRUCTION[6:0]; nop = out_20; PC_sel = PCsel; r_divu = DIVU_8; r_mul = MULT_10;
  //   r_mulh = MULH_14; r_mulhu = MULHU_11; REMU_9 = r_remu; SUB_12 = r_sub; s_sw = MEM_WE; sb_bltu = brUN;
  //   U = BSEL_13; u_lui = BSEL_13; uj_jal = UJ

  // Notes on the sheet:
  //   input
  //   split
  //   R_TYPE
  //   S_TYPE
  //   U_TYPE
  //   UJ_TYPE
  //   jump
  //   regWE
  //   OUTPUT
  //   type
  //   I_TYPE
  //   SB_TYPE
  //   ALU_SIGNAL
  //   WBsel
  //   0xFF1FF06F
  //   jal x0, func1
  //   0x00628463
  //   beq t0, t1, func2
  //   stack_type
  //   Asel
  //   Bsel
  //   PCsel
  //   brUN
endmodule

module lwc_com (
  input  [31:0] R2,
  output lwc_en
);

  wire comparator_1_eq;

  not not_1 (lwc_en, comparator_1_eq);
  Comparator #(.width(32), .mode("unsigned")) comparator_1 (
    .a(R2), .b({32{1'b0}}), .eq(comparator_1_eq));  // open: gt, lt

  // Other names for the same wires on the sheet: B[31:0] = R2
endmodule

module stack_instruction (
  input  [31:0] instruction,
  output [31:0] instruction_trans
);

  wire comparator_2_eq, comparator_3_eq, normal, pop, push, stacktype;
  wire [31:0] and_3_out, and_4_out, and_5_out, bit_extender_1_out, bit_extender_2_out, bit_extender_3_out;

  Comparator #(.width(7), .mode("unsigned")) comparator_1 (
    .a(instruction[6:0]), .b(7'b0111011), .eq(stacktype));  // open: gt, lt
  Comparator #(.width(3), .mode("unsigned")) comparator_2 (
    .a(instruction[14:12]), .b(3'b011), .eq(comparator_2_eq));  // open: gt, lt
  Comparator #(.width(3), .mode("unsigned")) comparator_3 (
    .a(instruction[14:12]), .b(3'b010), .eq(comparator_3_eq));  // open: gt, lt
  and and_1 (push, comparator_2_eq, stacktype);
  and and_2 (pop, comparator_3_eq, stacktype);
  not not_1 (normal, stacktype);
  assign bit_extender_1_out = {{31{push}}, push};  // Bit_Extender bit_extender_1
  assign bit_extender_2_out = {{31{pop}}, pop};  // Bit_Extender bit_extender_2
  assign bit_extender_3_out = {{31{normal}}, normal};  // Bit_Extender bit_extender_3
  assign and_3_out = {instruction[31:20], 5'b00010, instruction[14:0]} & bit_extender_1_out;  // AND_Gate and_3, 32 bits wide
  assign and_4_out = {instruction[31:20], 5'b00010, instruction[14:0]} & bit_extender_2_out;  // AND_Gate and_4, 32 bits wide
  assign and_5_out = instruction & bit_extender_3_out;  // AND_Gate and_5, 32 bits wide
  // Probe on instruction
  assign instruction_trans = and_3_out | and_4_out | and_5_out;  // OR_Gate or_1, 32 bits wide

  // Other names for the same wires on the sheet: instr[31:0] = instruction; intype[6:0] = instruction[6:0];
  //   ins_7 = instruction[7]; ins_11_7[4:0] = instruction[11:7]; ins_11_8[3:0] = instruction[11:8];
  //   func3[2:0] = instruction[14:12]; ins_19_12[7:0] = instruction[19:12]; ins_31_12[19:0] = instruction[31:12];
  //   ins_20 = instruction[20]; ins_30_20[10:0] = instruction[30:20]; ins_31_20[11:0] = instruction[31:20];
  //   rs2[4:0] = instruction[24:20]; ins_30_21[9:0] = instruction[30:21]; func7[6:0] = instruction[31:25];
  //   ins_30_25[5:0] = instruction[30:25]; ins_31 = instruction[31]; rs1[4:0] = instruction[19:15]
endmodule
